# Fritzing sketch Wiring (saved by Fritzing 0.9.3b)
breadboards: 1

parts:
  Raspberry_Pi_2 = Raspberry Pi 3 [part_number=RPI-3-V1.2]
  ISO = DB25F
  TRRS1 = Audio Jack (TRRS) 3.5mm [part_number="LUMBERG JEITA RC-5325A" package="RC-5325A [SMD]"]
  Bauteil1 = Arduino Nano (Rev3.0) (ICSP)
  ISO_1 = DB25F
  ISO_2 = DB25F

nets:
  N1: Raspberry_Pi_2.GPIO2, Bauteil1.A4
  N2: Raspberry_Pi_2.GPIO3, Bauteil1.A5
  GND: Raspberry_Pi_2.GND, Bauteil1.GND
  5V: Raspberry_Pi_2.5V, Bauteil1.5V
  N3: ISO.pin1, TRRS1.RING2
  N4: ISO.pin2, TRRS1.SLEEVE
  N5: ISO.pin3, TRRS1.TIP
  N6: ISO.pin8, Bauteil1.D13/SCK
  N7: ISO.pin9, Bauteil1.D12/MISO
  N8: ISO.pin10, Bauteil1.D11/MOSI
  N9: ISO_1.pin1, ISO_2.pin13
  N10: ISO_1.pin2, ISO_2.pin12
  N11: ISO_1.pin3, ISO_2.pin11
